# Fritzing sketch C029_uno+hall49E (saved by Fritzing 0.9.3b)
breadboards: 1

parts:
  Q1 = PNP-Transistor [package="TO92 [THT]"]
  R11 = Resistor [tolerance=±5% resistance=220 package=THT]
  LED5 = LED - 5mm [color="Yellow (595nm)" package="5 mm [THT]"]
  Composant2 = Arduino Uno (Rev3)

nets:
  N1: Q1.E, Composant2.5V
  N2: Q1.B, LED5.cathode, Composant2.GND
  N3: Q1.C, Composant2.A0
  N4: R11.Pin_0, Composant2.D8
  N5: R11.Pin_1, LED5.anode

notes:
  49E
